# Fritzing sketch rpi_button (saved by Fritzing 0.9.4)
breadboards: 1

parts:
  Raspberry_Pi_1 = Raspberry Pi 2
  S1 = Pushbutton [package="[THT]"]
  R1 = Resistor [tolerance=±5% resistance=10k package=THT]
  R2 = Resistor [tolerance=±5% resistance=1k package=THT]

nets:
  N1: Raspberry_Pi_1.3v3, S1.Pin_1, S1.Pin_2, R1.Pin_0, R2.Pin_0
  N2: Raspberry_Pi_1.GND, R1.Pin_1
  N3: Raspberry_Pi_1.GPIO23, R2.Pin_1
