# Fritzing sketch rpi_seven_segment (saved by Fritzing 0.9.4)
breadboards: 1

parts:
  Raspberry_Pi_1 = Raspberry Pi 2
  7_Segment1 = 7 Segment Display
  R2 = Resistor [tolerance=±5% resistance=100 package=THT]
  R3 = Resistor [tolerance=±5% resistance=100 package=THT]
  R4 = Resistor [tolerance=±5% resistance=100 package=THT]
  R5 = Resistor [tolerance=±5% resistance=100 package=THT]
  R6 = Resistor [tolerance=±5% resistance=100 package=THT]
  R7 = Resistor [tolerance=±5% resistance=100 package=THT]
  R8 = Resistor [tolerance=±5% resistance=100 package=THT]

nets:
  N1: Raspberry_Pi_1.GPIO17, R6.Pin_1
  N2: Raspberry_Pi_1.GPIO27, R8.Pin_0
  N3: Raspberry_Pi_1.GPIO22, R5.Pin_1
  N4: Raspberry_Pi_1.GPIO5, R7.Pin_0
  N5: Raspberry_Pi_1.GPIO6, R2.Pin_1
  N6: Raspberry_Pi_1.GPIO13, R4.Pin_0
  N7: Raspberry_Pi_1.GPIO19, R3.Pin_0
  N8: Raspberry_Pi_1.GND, 7_Segment1.common_cathode
  N9: 7_Segment1.Segment_E, R3.Pin_1
  N10: 7_Segment1.Segment_D, R4.Pin_1
  N11: 7_Segment1.Segment_C, R2.Pin_0
  N12: 7_Segment1.Segment_B, R5.Pin_0
  N13: 7_Segment1.Segment_A, R6.Pin_0
  N14: 7_Segment1.Segment_F, R8.Pin_1
  N15: 7_Segment1.Segment_G, R7.Pin_1
